// Logisim project NC16.circ as structural Verilog: 5 circuits, main circuit main
module main (
);

  wire alu_1_carry_flag, alu_1_sign_flag, alu_1_zero_flag, and_1_out, button_1_out, clock_1_out, not_1_out;
  wire [4:0] instruction_control_1_cpu_control_bus_2;
  wire [15:0] alu_1_alu_out, decoder_1_out0, demultiplexer_1_out0, demultiplexer_1_out1, dipswitch_1_sw16,
       instruction_control_1_mem_data_out, instruction_control_1_operand, instruction_control_1_pc_data_out,
       multiplexer_1_out, multiplexer_2_out, multiplexer_3_out, registers_1_a_out, registers_1_b_out,
       registers_1_bp_out, registers_1_c_out, registers_1_d_out, registers_1_e_out, registers_1_flag_output,
       registers_1_memaddr_out, registers_1_memval_out, registers_1_output_out, registers_1_sp_out;
  wire [18:0] instruction_control_1_cpu_control_bus;

  LedBar #(.matrixcols(16)) Output_port_LED (
    .led0(registers_1_output_out[15]), .led1(registers_1_output_out[14]), .led2(registers_1_output_out[13]),
    .led3(registers_1_output_out[12]), .led4(registers_1_output_out[11]), .led5(registers_1_output_out[10]),
    .led6(registers_1_output_out[9]), .led7(registers_1_output_out[8]), .led8(registers_1_output_out[7]),
    .led9(registers_1_output_out[6]), .led10(registers_1_output_out[5]), .led11(registers_1_output_out[4]),
    .led12(registers_1_output_out[3]), .led13(registers_1_output_out[2]), .led14(registers_1_output_out[1]),
    .led15(registers_1_output_out[0]));
  DipSwitch #(.number(16)) dipswitch_1 (
    .sw1(dipswitch_1_sw16[15]), .sw2(dipswitch_1_sw16[14]), .sw3(dipswitch_1_sw16[13]),
    .sw4(dipswitch_1_sw16[12]), .sw5(dipswitch_1_sw16[11]), .sw6(dipswitch_1_sw16[10]),
    .sw7(dipswitch_1_sw16[9]), .sw8(dipswitch_1_sw16[8]), .sw9(dipswitch_1_sw16[7]),
    .sw10(dipswitch_1_sw16[6]), .sw11(dipswitch_1_sw16[5]), .sw12(dipswitch_1_sw16[4]),
    .sw13(dipswitch_1_sw16[3]), .sw14(dipswitch_1_sw16[2]), .sw15(dipswitch_1_sw16[1]),
    .sw16(dipswitch_1_sw16[0]));
  Button button_1 (.out(button_1_out));
  Clock clock_1 (.out(clock_1_out));
  and and_1 (and_1_out, clock_1_out, not_1_out);
  Decoder #(.select(4)) decoder_1 (
    .out0(decoder_1_out0[0]), .out1(decoder_1_out0[1]), .out2(decoder_1_out0[2]), .out3(decoder_1_out0[3]),
    .out4(decoder_1_out0[4]), .out5(decoder_1_out0[5]), .out6(decoder_1_out0[6]), .out7(decoder_1_out0[7]),
    .out8(decoder_1_out0[8]), .out9(decoder_1_out0[9]), .out10(decoder_1_out0[10]),
    .out11(decoder_1_out0[11]), .out12(decoder_1_out0[12]), .out13(decoder_1_out0[13]),
    .out14(decoder_1_out0[14]), .out15(decoder_1_out0[15]), .sel(instruction_control_1_cpu_control_bus[5:2]));  // open: en
  registers registers_1 (
    .reg_data_in(multiplexer_2_out), .CLK(and_1_out), .RESET(button_1_out),
    .write_reg_select(decoder_1_out0), .carry_flag(alu_1_carry_flag), .zero_flag(alu_1_zero_flag),
    .sign_flag(alu_1_sign_flag), .flag_write_sw(instruction_control_1_cpu_control_bus[18]),
    .memval_out(registers_1_memval_out), .memaddr_out(registers_1_memaddr_out), .a_out(registers_1_a_out),
    .b_out(registers_1_b_out), .c_out(registers_1_c_out), .d_out(registers_1_d_out),
    .e_out(registers_1_e_out), .bp_out(registers_1_bp_out), .sp_out(registers_1_sp_out),
    .output_out(registers_1_output_out), .flag_output(registers_1_flag_output));
  Instruction_Control instruction_control_1 (
    .mem_data_in(registers_1_memval_out), .mem_addr_in(registers_1_memaddr_out), .CLK(and_1_out),
    .pc_data_in(multiplexer_2_out), .pc_write_enable(decoder_1_out0[7]),
    .carry_flag(registers_1_flag_output[0]), .zero_flag(registers_1_flag_output[1]),
    .sign_flag(registers_1_flag_output[2]), .RESET(button_1_out),
    .mem_data_out(instruction_control_1_mem_data_out), .operand(instruction_control_1_operand),
    .pc_data_out(instruction_control_1_pc_data_out),
    .CPU_Control_BUS({instruction_control_1_cpu_control_bus[18:17], instruction_control_1_cpu_control_bus_2, instruction_control_1_cpu_control_bus[11:0]}));
  Multiplexer #(.select(4), .width(16)) multiplexer_1 (
    .in0(registers_1_a_out), .in1(registers_1_b_out), .in2(registers_1_c_out), .in3(registers_1_d_out),
    .in4(registers_1_e_out), .in5(registers_1_bp_out), .in6(registers_1_sp_out),
    .in7(instruction_control_1_operand), .in8(dipswitch_1_sw16), .in9(instruction_control_1_mem_data_out),
    .in10(instruction_control_1_pc_data_out), .in11(registers_1_memval_out), .in12(registers_1_flag_output),
    .out(multiplexer_1_out), .sel(instruction_control_1_cpu_control_bus_2[4:1]));  // open: in13, in14, in15
  Demultiplexer #(.width(16)) demultiplexer_1 (
    .out0(demultiplexer_1_out0), .out1(demultiplexer_1_out1), .in(multiplexer_1_out),
    .sel(instruction_control_1_cpu_control_bus_2[0]));
  not not_1 (not_1_out, instruction_control_1_cpu_control_bus[17]);
  Multiplexer #(.width(16)) multiplexer_2 (
    .in0(demultiplexer_1_out0), .in1(alu_1_alu_out), .out(multiplexer_2_out),
    .sel(instruction_control_1_cpu_control_bus_2[0]));
  Multiplexer #(.select(3), .width(16)) multiplexer_3 (
    .in0(registers_1_a_out), .in1(registers_1_b_out), .in2(registers_1_c_out), .in3(registers_1_d_out),
    .in4(registers_1_e_out), .in5(registers_1_bp_out), .in6(registers_1_sp_out),
    .in7(instruction_control_1_operand), .out(multiplexer_3_out),
    .sel(instruction_control_1_cpu_control_bus[11:9]));
  ALU alu_1 (
    .in1_data_in(demultiplexer_1_out1), .in2_data_in(multiplexer_3_out),
    .ALU_function_select(instruction_control_1_cpu_control_bus[8:6]), .ALU_Out(alu_1_alu_out),
    .sign_flag(alu_1_sign_flag), .zero_flag(alu_1_zero_flag), .carry_flag(alu_1_carry_flag));
endmodule

module right_shifter (
  input  [15:0] Input_bus_1,
  input  [15:0] Input_bus_2,
  output carry_out,
  output [15:0] Output_bus_1
);

  wire and_1_out, and_2_out, and_3_out, and_4_out, and_5_out, and_6_out, and_7_out, and_8_out, and_9_out,
       and_10_out, and_11_out, and_12_out, and_13_out, and_14_out, and_15_out, or_1_out, or_2_out;
  wire [14:0] PLA_1_out;
  wire [15:0] multiplexer_1_out, multiplexer_17_out, multiplexer_33_out, multiplexer_49_out,
       multiplexer_65_out, multiplexer_81_out, multiplexer_97_out, multiplexer_113_out, multiplexer_129_out,
       multiplexer_145_out, multiplexer_161_out, multiplexer_177_out, multiplexer_193_out,
       multiplexer_225_out;

  PLA #(.in_width(16), .out_width(15), .\table ("0000000000000001 000000000000001 # 1\n0000000000000010 000000000000011 # 2\n0000000000000011 000000000000111 # 3\n0000000000000100 000000000001111 # 4\n0000000000000101 000000000011111 # 5\n0000000000000110 000000000111111 # 6\n0000000000000111 000000001111111 # 7\n0000000000001000 000000011111111 # 8\n0000000000001001 000000111111111 # 9\n0000000000001010 000001111111111 # 10\n0000000000001011 000011111111111 # 11\n0000000000001100 000111111111111 # 12\n0000000000001101 001111111111111 # 13\n0000000000001110 011111111111111 # 14\n0000000000001111 111111111111111 # 15")) PLA_1 (
    .in(Input_bus_1), .out(PLA_1_out));
  and and_1 (and_1_out, Input_bus_2[0], PLA_1_out[0]);
  Multiplexer multiplexer_1 (
    .in0(Input_bus_2[0]), .in1(Input_bus_2[1]), .out(multiplexer_1_out[0]), .sel(PLA_1_out[0]));
  Multiplexer multiplexer_2 (
    .in0(Input_bus_2[1]), .in1(Input_bus_2[2]), .out(multiplexer_1_out[1]), .sel(PLA_1_out[0]));
  Multiplexer multiplexer_3 (
    .in0(Input_bus_2[2]), .in1(Input_bus_2[3]), .out(multiplexer_1_out[2]), .sel(PLA_1_out[0]));
  Multiplexer multiplexer_4 (
    .in0(Input_bus_2[3]), .in1(Input_bus_2[4]), .out(multiplexer_1_out[3]), .sel(PLA_1_out[0]));
  Multiplexer multiplexer_5 (
    .in0(Input_bus_2[4]), .in1(Input_bus_2[5]), .out(multiplexer_1_out[4]), .sel(PLA_1_out[0]));
  Multiplexer multiplexer_6 (
    .in0(Input_bus_2[5]), .in1(Input_bus_2[6]), .out(multiplexer_1_out[5]), .sel(PLA_1_out[0]));
  Multiplexer multiplexer_7 (
    .in0(Input_bus_2[6]), .in1(Input_bus_2[7]), .out(multiplexer_1_out[6]), .sel(PLA_1_out[0]));
  Multiplexer multiplexer_8 (
    .in0(Input_bus_2[7]), .in1(Input_bus_2[8]), .out(multiplexer_1_out[7]), .sel(PLA_1_out[0]));
  Multiplexer multiplexer_9 (
    .in0(Input_bus_2[8]), .in1(Input_bus_2[9]), .out(multiplexer_1_out[8]), .sel(PLA_1_out[0]));
  Multiplexer multiplexer_10 (
    .in0(Input_bus_2[9]), .in1(Input_bus_2[10]), .out(multiplexer_1_out[9]), .sel(PLA_1_out[0]));
  Multiplexer multiplexer_11 (
    .in0(Input_bus_2[10]), .in1(Input_bus_2[11]), .out(multiplexer_1_out[10]), .sel(PLA_1_out[0]));
  Multiplexer multiplexer_12 (
    .in0(Input_bus_2[11]), .in1(Input_bus_2[12]), .out(multiplexer_1_out[11]), .sel(PLA_1_out[0]));
  Multiplexer multiplexer_13 (
    .in0(Input_bus_2[12]), .in1(Input_bus_2[13]), .out(multiplexer_1_out[12]), .sel(PLA_1_out[0]));
  Multiplexer multiplexer_14 (
    .in0(Input_bus_2[13]), .in1(Input_bus_2[14]), .out(multiplexer_1_out[13]), .sel(PLA_1_out[0]));
  Multiplexer multiplexer_15 (
    .in0(Input_bus_2[14]), .in1(Input_bus_2[15]), .out(multiplexer_1_out[14]), .sel(PLA_1_out[0]));
  Multiplexer multiplexer_16 (.in0(Input_bus_2[15]), .in1(1'b0), .out(multiplexer_1_out[15]), .sel(PLA_1_out[0]));
  and and_2 (and_2_out, multiplexer_225_out[0], PLA_1_out[8]);
  Multiplexer multiplexer_17 (
    .in0(multiplexer_225_out[0]), .in1(multiplexer_225_out[1]), .out(multiplexer_17_out[0]),
    .sel(PLA_1_out[8]));
  Multiplexer multiplexer_18 (
    .in0(multiplexer_225_out[1]), .in1(multiplexer_225_out[2]), .out(multiplexer_17_out[1]),
    .sel(PLA_1_out[8]));
  Multiplexer multiplexer_19 (
    .in0(multiplexer_225_out[2]), .in1(multiplexer_225_out[3]), .out(multiplexer_17_out[2]),
    .sel(PLA_1_out[8]));
  Multiplexer multiplexer_20 (
    .in0(multiplexer_225_out[3]), .in1(multiplexer_225_out[4]), .out(multiplexer_17_out[3]),
    .sel(PLA_1_out[8]));
  Multiplexer multiplexer_21 (
    .in0(multiplexer_225_out[4]), .in1(multiplexer_225_out[5]), .out(multiplexer_17_out[4]),
    .sel(PLA_1_out[8]));
  Multiplexer multiplexer_22 (
    .in0(multiplexer_225_out[5]), .in1(multiplexer_225_out[6]), .out(multiplexer_17_out[5]),
    .sel(PLA_1_out[8]));
  Multiplexer multiplexer_23 (
    .in0(multiplexer_225_out[6]), .in1(multiplexer_225_out[7]), .out(multiplexer_17_out[6]),
    .sel(PLA_1_out[8]));
  Multiplexer multiplexer_24 (
    .in0(multiplexer_225_out[7]), .in1(multiplexer_225_out[8]), .out(multiplexer_17_out[7]),
    .sel(PLA_1_out[8]));
  Multiplexer multiplexer_25 (
    .in0(multiplexer_225_out[8]), .in1(multiplexer_225_out[9]), .out(multiplexer_17_out[8]),
    .sel(PLA_1_out[8]));
  Multiplexer multiplexer_26 (
    .in0(multiplexer_225_out[9]), .in1(multiplexer_225_out[10]), .out(multiplexer_17_out[9]),
    .sel(PLA_1_out[8]));
  Multiplexer multiplexer_27 (
    .in0(multiplexer_225_out[10]), .in1(multiplexer_225_out[11]), .out(multiplexer_17_out[10]),
    .sel(PLA_1_out[8]));
  Multiplexer multiplexer_28 (
    .in0(multiplexer_225_out[11]), .in1(multiplexer_225_out[12]), .out(multiplexer_17_out[11]),
    .sel(PLA_1_out[8]));
  Multiplexer multiplexer_29 (
    .in0(multiplexer_225_out[12]), .in1(multiplexer_225_out[13]), .out(multiplexer_17_out[12]),
    .sel(PLA_1_out[8]));
  Multiplexer multiplexer_30 (
    .in0(multiplexer_225_out[13]), .in1(multiplexer_225_out[14]), .out(multiplexer_17_out[13]),
    .sel(PLA_1_out[8]));
  Multiplexer multiplexer_31 (
    .in0(multiplexer_225_out[14]), .in1(multiplexer_225_out[15]), .out(multiplexer_17_out[14]),
    .sel(PLA_1_out[8]));
  Multiplexer multiplexer_32 (
    .in0(multiplexer_225_out[15]), .in1(1'b0), .out(multiplexer_17_out[15]), .sel(PLA_1_out[8]));
  and and_3 (and_3_out, multiplexer_1_out[0], PLA_1_out[1]);
  and and_4 (and_4_out, multiplexer_17_out[0], PLA_1_out[9]);
  Multiplexer multiplexer_33 (
    .in0(multiplexer_1_out[0]), .in1(multiplexer_1_out[1]), .out(multiplexer_33_out[0]), .sel(PLA_1_out[1]));
  Multiplexer multiplexer_34 (
    .in0(multiplexer_1_out[1]), .in1(multiplexer_1_out[2]), .out(multiplexer_33_out[1]), .sel(PLA_1_out[1]));
  Multiplexer multiplexer_35 (
    .in0(multiplexer_1_out[2]), .in1(multiplexer_1_out[3]), .out(multiplexer_33_out[2]), .sel(PLA_1_out[1]));
  Multiplexer multiplexer_36 (
    .in0(multiplexer_1_out[3]), .in1(multiplexer_1_out[4]), .out(multiplexer_33_out[3]), .sel(PLA_1_out[1]));
  Multiplexer multiplexer_37 (
    .in0(multiplexer_1_out[4]), .in1(multiplexer_1_out[5]), .out(multiplexer_33_out[4]), .sel(PLA_1_out[1]));
  Multiplexer multiplexer_38 (
    .in0(multiplexer_1_out[5]), .in1(multiplexer_1_out[6]), .out(multiplexer_33_out[5]), .sel(PLA_1_out[1]));
  Multiplexer multiplexer_39 (
    .in0(multiplexer_1_out[6]), .in1(multiplexer_1_out[7]), .out(multiplexer_33_out[6]), .sel(PLA_1_out[1]));
  Multiplexer multiplexer_40 (
    .in0(multiplexer_1_out[7]), .in1(multiplexer_1_out[8]), .out(multiplexer_33_out[7]), .sel(PLA_1_out[1]));
  Multiplexer multiplexer_41 (
    .in0(multiplexer_1_out[8]), .in1(multiplexer_1_out[9]), .out(multiplexer_33_out[8]), .sel(PLA_1_out[1]));
  Multiplexer multiplexer_42 (
    .in0(multiplexer_1_out[9]), .in1(multiplexer_1_out[10]), .out(multiplexer_33_out[9]), .sel(PLA_1_out[1]));
  Multiplexer multiplexer_43 (
    .in0(multiplexer_1_out[10]), .in1(multiplexer_1_out[11]), .out(multiplexer_33_out[10]), .sel(PLA_1_out[1]));
  Multiplexer multiplexer_44 (
    .in0(multiplexer_1_out[11]), .in1(multiplexer_1_out[12]), .out(multiplexer_33_out[11]), .sel(PLA_1_out[1]));
  Multiplexer multiplexer_45 (
    .in0(multiplexer_1_out[12]), .in1(multiplexer_1_out[13]), .out(multiplexer_33_out[12]), .sel(PLA_1_out[1]));
  Multiplexer multiplexer_46 (
    .in0(multiplexer_1_out[13]), .in1(multiplexer_1_out[14]), .out(multiplexer_33_out[13]), .sel(PLA_1_out[1]));
  Multiplexer multiplexer_47 (
    .in0(multiplexer_1_out[14]), .in1(multiplexer_1_out[15]), .out(multiplexer_33_out[14]), .sel(PLA_1_out[1]));
  Multiplexer multiplexer_48 (
    .in0(multiplexer_1_out[15]), .in1(1'b0), .out(multiplexer_33_out[15]), .sel(PLA_1_out[1]));
  Multiplexer multiplexer_49 (
    .in0(multiplexer_17_out[0]), .in1(multiplexer_17_out[1]), .out(multiplexer_49_out[0]), .sel(PLA_1_out[9]));
  Multiplexer multiplexer_50 (
    .in0(multiplexer_17_out[1]), .in1(multiplexer_17_out[2]), .out(multiplexer_49_out[1]), .sel(PLA_1_out[9]));
  Multiplexer multiplexer_51 (
    .in0(multiplexer_17_out[2]), .in1(multiplexer_17_out[3]), .out(multiplexer_49_out[2]), .sel(PLA_1_out[9]));
  Multiplexer multiplexer_52 (
    .in0(multiplexer_17_out[3]), .in1(multiplexer_17_out[4]), .out(multiplexer_49_out[3]), .sel(PLA_1_out[9]));
  Multiplexer multiplexer_53 (
    .in0(multiplexer_17_out[4]), .in1(multiplexer_17_out[5]), .out(multiplexer_49_out[4]), .sel(PLA_1_out[9]));
  Multiplexer multiplexer_54 (
    .in0(multiplexer_17_out[5]), .in1(multiplexer_17_out[6]), .out(multiplexer_49_out[5]), .sel(PLA_1_out[9]));
  Multiplexer multiplexer_55 (
    .in0(multiplexer_17_out[6]), .in1(multiplexer_17_out[7]), .out(multiplexer_49_out[6]), .sel(PLA_1_out[9]));
  Multiplexer multiplexer_56 (
    .in0(multiplexer_17_out[7]), .in1(multiplexer_17_out[8]), .out(multiplexer_49_out[7]), .sel(PLA_1_out[9]));
  Multiplexer multiplexer_57 (
    .in0(multiplexer_17_out[8]), .in1(multiplexer_17_out[9]), .out(multiplexer_49_out[8]), .sel(PLA_1_out[9]));
  Multiplexer multiplexer_58 (
    .in0(multiplexer_17_out[9]), .in1(multiplexer_17_out[10]), .out(multiplexer_49_out[9]), .sel(PLA_1_out[9]));
  Multiplexer multiplexer_59 (
    .in0(multiplexer_17_out[10]), .in1(multiplexer_17_out[11]), .out(multiplexer_49_out[10]),
    .sel(PLA_1_out[9]));
  Multiplexer multiplexer_60 (
    .in0(multiplexer_17_out[11]), .in1(multiplexer_17_out[12]), .out(multiplexer_49_out[11]),
    .sel(PLA_1_out[9]));
  Multiplexer multiplexer_61 (
    .in0(multiplexer_17_out[12]), .in1(multiplexer_17_out[13]), .out(multiplexer_49_out[12]),
    .sel(PLA_1_out[9]));
  Multiplexer multiplexer_62 (
    .in0(multiplexer_17_out[13]), .in1(multiplexer_17_out[14]), .out(multiplexer_49_out[13]),
    .sel(PLA_1_out[9]));
  Multiplexer multiplexer_63 (
    .in0(multiplexer_17_out[14]), .in1(multiplexer_17_out[15]), .out(multiplexer_49_out[14]),
    .sel(PLA_1_out[9]));
  Multiplexer multiplexer_64 (
    .in0(multiplexer_17_out[15]), .in1(1'b0), .out(multiplexer_49_out[15]), .sel(PLA_1_out[9]));
  and and_5 (and_5_out, multiplexer_33_out[0], PLA_1_out[2]);
  Multiplexer multiplexer_65 (
    .in0(multiplexer_33_out[0]), .in1(multiplexer_33_out[1]), .out(multiplexer_65_out[0]), .sel(PLA_1_out[2]));
  Multiplexer multiplexer_66 (
    .in0(multiplexer_33_out[1]), .in1(multiplexer_33_out[2]), .out(multiplexer_65_out[1]), .sel(PLA_1_out[2]));
  Multiplexer multiplexer_67 (
    .in0(multiplexer_33_out[2]), .in1(multiplexer_33_out[3]), .out(multiplexer_65_out[2]), .sel(PLA_1_out[2]));
  Multiplexer multiplexer_68 (
    .in0(multiplexer_33_out[3]), .in1(multiplexer_33_out[4]), .out(multiplexer_65_out[3]), .sel(PLA_1_out[2]));
  Multiplexer multiplexer_69 (
    .in0(multiplexer_33_out[4]), .in1(multiplexer_33_out[5]), .out(multiplexer_65_out[4]), .sel(PLA_1_out[2]));
  Multiplexer multiplexer_70 (
    .in0(multiplexer_33_out[5]), .in1(multiplexer_33_out[6]), .out(multiplexer_65_out[5]), .sel(PLA_1_out[2]));
  Multiplexer multiplexer_71 (
    .in0(multiplexer_33_out[6]), .in1(multiplexer_33_out[7]), .out(multiplexer_65_out[6]), .sel(PLA_1_out[2]));
  Multiplexer multiplexer_72 (
    .in0(multiplexer_33_out[7]), .in1(multiplexer_33_out[8]), .out(multiplexer_65_out[7]), .sel(PLA_1_out[2]));
  Multiplexer multiplexer_73 (
    .in0(multiplexer_33_out[8]), .in1(multiplexer_33_out[9]), .out(multiplexer_65_out[8]), .sel(PLA_1_out[2]));
  Multiplexer multiplexer_74 (
    .in0(multiplexer_33_out[9]), .in1(multiplexer_33_out[10]), .out(multiplexer_65_out[9]), .sel(PLA_1_out[2]));
  Multiplexer multiplexer_75 (
    .in0(multiplexer_33_out[10]), .in1(multiplexer_33_out[11]), .out(multiplexer_65_out[10]),
    .sel(PLA_1_out[2]));
  Multiplexer multiplexer_76 (
    .in0(multiplexer_33_out[11]), .in1(multiplexer_33_out[12]), .out(multiplexer_65_out[11]),
    .sel(PLA_1_out[2]));
  Multiplexer multiplexer_77 (
    .in0(multiplexer_33_out[12]), .in1(multiplexer_33_out[13]), .out(multiplexer_65_out[12]),
    .sel(PLA_1_out[2]));
  Multiplexer multiplexer_78 (
    .in0(multiplexer_33_out[13]), .in1(multiplexer_33_out[14]), .out(multiplexer_65_out[13]),
    .sel(PLA_1_out[2]));
  Multiplexer multiplexer_79 (
    .in0(multiplexer_33_out[14]), .in1(multiplexer_33_out[15]), .out(multiplexer_65_out[14]),
    .sel(PLA_1_out[2]));
  Multiplexer multiplexer_80 (
    .in0(multiplexer_33_out[15]), .in1(1'b0), .out(multiplexer_65_out[15]), .sel(PLA_1_out[2]));
  and and_6 (and_6_out, multiplexer_49_out[0], PLA_1_out[10]);
  Multiplexer multiplexer_81 (
    .in0(multiplexer_49_out[0]), .in1(multiplexer_49_out[1]), .out(multiplexer_81_out[0]), .sel(PLA_1_out[10]));
  Multiplexer multiplexer_82 (
    .in0(multiplexer_49_out[1]), .in1(multiplexer_49_out[2]), .out(multiplexer_81_out[1]), .sel(PLA_1_out[10]));
  Multiplexer multiplexer_83 (
    .in0(multiplexer_49_out[2]), .in1(multiplexer_49_out[3]), .out(multiplexer_81_out[2]), .sel(PLA_1_out[10]));
  Multiplexer multiplexer_84 (
    .in0(multiplexer_49_out[3]), .in1(multiplexer_49_out[4]), .out(multiplexer_81_out[3]), .sel(PLA_1_out[10]));
  Multiplexer multiplexer_85 (
    .in0(multiplexer_49_out[4]), .in1(multiplexer_49_out[5]), .out(multiplexer_81_out[4]), .sel(PLA_1_out[10]));
  Multiplexer multiplexer_86 (
    .in0(multiplexer_49_out[5]), .in1(multiplexer_49_out[6]), .out(multiplexer_81_out[5]), .sel(PLA_1_out[10]));
  Multiplexer multiplexer_87 (
    .in0(multiplexer_49_out[6]), .in1(multiplexer_49_out[7]), .out(multiplexer_81_out[6]), .sel(PLA_1_out[10]));
  Multiplexer multiplexer_88 (
    .in0(multiplexer_49_out[7]), .in1(multiplexer_49_out[8]), .out(multiplexer_81_out[7]), .sel(PLA_1_out[10]));
  Multiplexer multiplexer_89 (
    .in0(multiplexer_49_out[8]), .in1(multiplexer_49_out[9]), .out(multiplexer_81_out[8]), .sel(PLA_1_out[10]));
  Multiplexer multiplexer_90 (
    .in0(multiplexer_49_out[9]), .in1(multiplexer_49_out[10]), .out(multiplexer_81_out[9]),
    .sel(PLA_1_out[10]));
  Multiplexer multiplexer_91 (
    .in0(multiplexer_49_out[10]), .in1(multiplexer_49_out[11]), .out(multiplexer_81_out[10]),
    .sel(PLA_1_out[10]));
  Multiplexer multiplexer_92 (
    .in0(multiplexer_49_out[11]), .in1(multiplexer_49_out[12]), .out(multiplexer_81_out[11]),
    .sel(PLA_1_out[10]));
  Multiplexer multiplexer_93 (
    .in0(multiplexer_49_out[12]), .in1(multiplexer_49_out[13]), .out(multiplexer_81_out[12]),
    .sel(PLA_1_out[10]));
  Multiplexer multiplexer_94 (
    .in0(multiplexer_49_out[13]), .in1(multiplexer_49_out[14]), .out(multiplexer_81_out[13]),
    .sel(PLA_1_out[10]));
  Multiplexer multiplexer_95 (
    .in0(multiplexer_49_out[14]), .in1(multiplexer_49_out[15]), .out(multiplexer_81_out[14]),
    .sel(PLA_1_out[10]));
  Multiplexer multiplexer_96 (
    .in0(multiplexer_49_out[15]), .in1(1'b0), .out(multiplexer_81_out[15]), .sel(PLA_1_out[10]));
  and and_7 (and_7_out, multiplexer_65_out[0], PLA_1_out[3]);
  Multiplexer multiplexer_97 (
    .in0(multiplexer_65_out[0]), .in1(multiplexer_65_out[1]), .out(multiplexer_97_out[0]), .sel(PLA_1_out[3]));
  Multiplexer multiplexer_98 (
    .in0(multiplexer_65_out[1]), .in1(multiplexer_65_out[2]), .out(multiplexer_97_out[1]), .sel(PLA_1_out[3]));
  Multiplexer multiplexer_99 (
    .in0(multiplexer_65_out[2]), .in1(multiplexer_65_out[3]), .out(multiplexer_97_out[2]), .sel(PLA_1_out[3]));
  Multiplexer multiplexer_100 (
    .in0(multiplexer_65_out[3]), .in1(multiplexer_65_out[4]), .out(multiplexer_97_out[3]), .sel(PLA_1_out[3]));
  Multiplexer multiplexer_101 (
    .in0(multiplexer_65_out[4]), .in1(multiplexer_65_out[5]), .out(multiplexer_97_out[4]), .sel(PLA_1_out[3]));
  Multiplexer multiplexer_102 (
    .in0(multiplexer_65_out[5]), .in1(multiplexer_65_out[6]), .out(multiplexer_97_out[5]), .sel(PLA_1_out[3]));
  Multiplexer multiplexer_103 (
    .in0(multiplexer_65_out[6]), .in1(multiplexer_65_out[7]), .out(multiplexer_97_out[6]), .sel(PLA_1_out[3]));
  Multiplexer multiplexer_104 (
    .in0(multiplexer_65_out[7]), .in1(multiplexer_65_out[8]), .out(multiplexer_97_out[7]), .sel(PLA_1_out[3]));
  Multiplexer multiplexer_105 (
    .in0(multiplexer_65_out[8]), .in1(multiplexer_65_out[9]), .out(multiplexer_97_out[8]), .sel(PLA_1_out[3]));
  Multiplexer multiplexer_106 (
    .in0(multiplexer_65_out[9]), .in1(multiplexer_65_out[10]), .out(multiplexer_97_out[9]), .sel(PLA_1_out[3]));
  Multiplexer multiplexer_107 (
    .in0(multiplexer_65_out[10]), .in1(multiplexer_65_out[11]), .out(multiplexer_97_out[10]),
    .sel(PLA_1_out[3]));
  Multiplexer multiplexer_108 (
    .in0(multiplexer_65_out[11]), .in1(multiplexer_65_out[12]), .out(multiplexer_97_out[11]),
    .sel(PLA_1_out[3]));
  Multiplexer multiplexer_109 (
    .in0(multiplexer_65_out[12]), .in1(multiplexer_65_out[13]), .out(multiplexer_97_out[12]),
    .sel(PLA_1_out[3]));
  Multiplexer multiplexer_110 (
    .in0(multiplexer_65_out[13]), .in1(multiplexer_65_out[14]), .out(multiplexer_97_out[13]),
    .sel(PLA_1_out[3]));
  Multiplexer multiplexer_111 (
    .in0(multiplexer_65_out[14]), .in1(multiplexer_65_out[15]), .out(multiplexer_97_out[14]),
    .sel(PLA_1_out[3]));
  Multiplexer multiplexer_112 (
    .in0(multiplexer_65_out[15]), .in1(1'b0), .out(multiplexer_97_out[15]), .sel(PLA_1_out[3]));
  and and_8 (and_8_out, multiplexer_81_out[0], PLA_1_out[11]);
  Multiplexer multiplexer_113 (
    .in0(multiplexer_81_out[0]), .in1(multiplexer_81_out[1]), .out(multiplexer_113_out[0]),
    .sel(PLA_1_out[11]));
  Multiplexer multiplexer_114 (
    .in0(multiplexer_81_out[1]), .in1(multiplexer_81_out[2]), .out(multiplexer_113_out[1]),
    .sel(PLA_1_out[11]));
  Multiplexer multiplexer_115 (
    .in0(multiplexer_81_out[2]), .in1(multiplexer_81_out[3]), .out(multiplexer_113_out[2]),
    .sel(PLA_1_out[11]));
  Multiplexer multiplexer_116 (
    .in0(multiplexer_81_out[3]), .in1(multiplexer_81_out[4]), .out(multiplexer_113_out[3]),
    .sel(PLA_1_out[11]));
  Multiplexer multiplexer_117 (
    .in0(multiplexer_81_out[4]), .in1(multiplexer_81_out[5]), .out(multiplexer_113_out[4]),
    .sel(PLA_1_out[11]));
  Multiplexer multiplexer_118 (
    .in0(multiplexer_81_out[5]), .in1(multiplexer_81_out[6]), .out(multiplexer_113_out[5]),
    .sel(PLA_1_out[11]));
  Multiplexer multiplexer_119 (
    .in0(multiplexer_81_out[6]), .in1(multiplexer_81_out[7]), .out(multiplexer_113_out[6]),
    .sel(PLA_1_out[11]));
  Multiplexer multiplexer_120 (
    .in0(multiplexer_81_out[7]), .in1(multiplexer_81_out[8]), .out(multiplexer_113_out[7]),
    .sel(PLA_1_out[11]));
  Multiplexer multiplexer_121 (
    .in0(multiplexer_81_out[8]), .in1(multiplexer_81_out[9]), .out(multiplexer_113_out[8]),
    .sel(PLA_1_out[11]));
  Multiplexer multiplexer_122 (
    .in0(multiplexer_81_out[9]), .in1(multiplexer_81_out[10]), .out(multiplexer_113_out[9]),
    .sel(PLA_1_out[11]));
  Multiplexer multiplexer_123 (
    .in0(multiplexer_81_out[10]), .in1(multiplexer_81_out[11]), .out(multiplexer_113_out[10]),
    .sel(PLA_1_out[11]));
  Multiplexer multiplexer_124 (
    .in0(multiplexer_81_out[11]), .in1(multiplexer_81_out[12]), .out(multiplexer_113_out[11]),
    .sel(PLA_1_out[11]));
  Multiplexer multiplexer_125 (
    .in0(multiplexer_81_out[12]), .in1(multiplexer_81_out[13]), .out(multiplexer_113_out[12]),
    .sel(PLA_1_out[11]));
  Multiplexer multiplexer_126 (
    .in0(multiplexer_81_out[13]), .in1(multiplexer_81_out[14]), .out(multiplexer_113_out[13]),
    .sel(PLA_1_out[11]));
  Multiplexer multiplexer_127 (
    .in0(multiplexer_81_out[14]), .in1(multiplexer_81_out[15]), .out(multiplexer_113_out[14]),
    .sel(PLA_1_out[11]));
  Multiplexer multiplexer_128 (
    .in0(multiplexer_81_out[15]), .in1(1'b0), .out(multiplexer_113_out[15]), .sel(PLA_1_out[11]));
  and and_9 (and_9_out, multiplexer_97_out[0], PLA_1_out[4]);
  Multiplexer multiplexer_129 (
    .in0(multiplexer_97_out[0]), .in1(multiplexer_97_out[1]), .out(multiplexer_129_out[0]), .sel(PLA_1_out[4]));
  Multiplexer multiplexer_130 (
    .in0(multiplexer_97_out[1]), .in1(multiplexer_97_out[2]), .out(multiplexer_129_out[1]), .sel(PLA_1_out[4]));
  Multiplexer multiplexer_131 (
    .in0(multiplexer_97_out[2]), .in1(multiplexer_97_out[3]), .out(multiplexer_129_out[2]), .sel(PLA_1_out[4]));
  Multiplexer multiplexer_132 (
    .in0(multiplexer_97_out[3]), .in1(multiplexer_97_out[4]), .out(multiplexer_129_out[3]), .sel(PLA_1_out[4]));
  Multiplexer multiplexer_133 (
    .in0(multiplexer_97_out[4]), .in1(multiplexer_97_out[5]), .out(multiplexer_129_out[4]), .sel(PLA_1_out[4]));
  Multiplexer multiplexer_134 (
    .in0(multiplexer_97_out[5]), .in1(multiplexer_97_out[6]), .out(multiplexer_129_out[5]), .sel(PLA_1_out[4]));
  Multiplexer multiplexer_135 (
    .in0(multiplexer_97_out[6]), .in1(multiplexer_97_out[7]), .out(multiplexer_129_out[6]), .sel(PLA_1_out[4]));
  Multiplexer multiplexer_136 (
    .in0(multiplexer_97_out[7]), .in1(multiplexer_97_out[8]), .out(multiplexer_129_out[7]), .sel(PLA_1_out[4]));
  Multiplexer multiplexer_137 (
    .in0(multiplexer_97_out[8]), .in1(multiplexer_97_out[9]), .out(multiplexer_129_out[8]), .sel(PLA_1_out[4]));
  Multiplexer multiplexer_138 (
    .in0(multiplexer_97_out[9]), .in1(multiplexer_97_out[10]), .out(multiplexer_129_out[9]),
    .sel(PLA_1_out[4]));
  Multiplexer multiplexer_139 (
    .in0(multiplexer_97_out[10]), .in1(multiplexer_97_out[11]), .out(multiplexer_129_out[10]),
    .sel(PLA_1_out[4]));
  Multiplexer multiplexer_140 (
    .in0(multiplexer_97_out[11]), .in1(multiplexer_97_out[12]), .out(multiplexer_129_out[11]),
    .sel(PLA_1_out[4]));
  Multiplexer multiplexer_141 (
    .in0(multiplexer_97_out[12]), .in1(multiplexer_97_out[13]), .out(multiplexer_129_out[12]),
    .sel(PLA_1_out[4]));
  Multiplexer multiplexer_142 (
    .in0(multiplexer_97_out[13]), .in1(multiplexer_97_out[14]), .out(multiplexer_129_out[13]),
    .sel(PLA_1_out[4]));
  Multiplexer multiplexer_143 (
    .in0(multiplexer_97_out[14]), .in1(multiplexer_97_out[15]), .out(multiplexer_129_out[14]),
    .sel(PLA_1_out[4]));
  Multiplexer multiplexer_144 (
    .in0(multiplexer_97_out[15]), .in1(1'b0), .out(multiplexer_129_out[15]), .sel(PLA_1_out[4]));
  and and_10 (and_10_out, multiplexer_113_out[0], PLA_1_out[12]);
  Multiplexer multiplexer_145 (
    .in0(multiplexer_113_out[0]), .in1(multiplexer_113_out[1]), .out(multiplexer_145_out[0]),
    .sel(PLA_1_out[12]));
  Multiplexer multiplexer_146 (
    .in0(multiplexer_113_out[1]), .in1(multiplexer_113_out[2]), .out(multiplexer_145_out[1]),
    .sel(PLA_1_out[12]));
  Multiplexer multiplexer_147 (
    .in0(multiplexer_113_out[2]), .in1(multiplexer_113_out[3]), .out(multiplexer_145_out[2]),
    .sel(PLA_1_out[12]));
  Multiplexer multiplexer_148 (
    .in0(multiplexer_113_out[3]), .in1(multiplexer_113_out[4]), .out(multiplexer_145_out[3]),
    .sel(PLA_1_out[12]));
  Multiplexer multiplexer_149 (
    .in0(multiplexer_113_out[4]), .in1(multiplexer_113_out[5]), .out(multiplexer_145_out[4]),
    .sel(PLA_1_out[12]));
  Multiplexer multiplexer_150 (
    .in0(multiplexer_113_out[5]), .in1(multiplexer_113_out[6]), .out(multiplexer_145_out[5]),
    .sel(PLA_1_out[12]));
  Multiplexer multiplexer_151 (
    .in0(multiplexer_113_out[6]), .in1(multiplexer_113_out[7]), .out(multiplexer_145_out[6]),
    .sel(PLA_1_out[12]));
  Multiplexer multiplexer_152 (
    .in0(multiplexer_113_out[7]), .in1(multiplexer_113_out[8]), .out(multiplexer_145_out[7]),
    .sel(PLA_1_out[12]));
  Multiplexer multiplexer_153 (
    .in0(multiplexer_113_out[8]), .in1(multiplexer_113_out[9]), .out(multiplexer_145_out[8]),
    .sel(PLA_1_out[12]));
  Multiplexer multiplexer_154 (
    .in0(multiplexer_113_out[9]), .in1(multiplexer_113_out[10]), .out(multiplexer_145_out[9]),
    .sel(PLA_1_out[12]));
  Multiplexer multiplexer_155 (
    .in0(multiplexer_113_out[10]), .in1(multiplexer_113_out[11]), .out(multiplexer_145_out[10]),
    .sel(PLA_1_out[12]));
  Multiplexer multiplexer_156 (
    .in0(multiplexer_113_out[11]), .in1(multiplexer_113_out[12]), .out(multiplexer_145_out[11]),
    .sel(PLA_1_out[12]));
  Multiplexer multiplexer_157 (
    .in0(multiplexer_113_out[12]), .in1(multiplexer_113_out[13]), .out(multiplexer_145_out[12]),
    .sel(PLA_1_out[12]));
  Multiplexer multiplexer_158 (
    .in0(multiplexer_113_out[13]), .in1(multiplexer_113_out[14]), .out(multiplexer_145_out[13]),
    .sel(PLA_1_out[12]));
  Multiplexer multiplexer_159 (
    .in0(multiplexer_113_out[14]), .in1(multiplexer_113_out[15]), .out(multiplexer_145_out[14]),
    .sel(PLA_1_out[12]));
  Multiplexer multiplexer_160 (
    .in0(multiplexer_113_out[15]), .in1(1'b0), .out(multiplexer_145_out[15]), .sel(PLA_1_out[12]));
  and and_11 (and_11_out, multiplexer_129_out[0], PLA_1_out[5]);
  Multiplexer multiplexer_161 (
    .in0(multiplexer_129_out[0]), .in1(multiplexer_129_out[1]), .out(multiplexer_161_out[0]),
    .sel(PLA_1_out[5]));
  Multiplexer multiplexer_162 (
    .in0(multiplexer_129_out[1]), .in1(multiplexer_129_out[2]), .out(multiplexer_161_out[1]),
    .sel(PLA_1_out[5]));
  Multiplexer multiplexer_163 (
    .in0(multiplexer_129_out[2]), .in1(multiplexer_129_out[3]), .out(multiplexer_161_out[2]),
    .sel(PLA_1_out[5]));
  Multiplexer multiplexer_164 (
    .in0(multiplexer_129_out[3]), .in1(multiplexer_129_out[4]), .out(multiplexer_161_out[3]),
    .sel(PLA_1_out[5]));
  Multiplexer multiplexer_165 (
    .in0(multiplexer_129_out[4]), .in1(multiplexer_129_out[5]), .out(multiplexer_161_out[4]),
    .sel(PLA_1_out[5]));
  Multiplexer multiplexer_166 (
    .in0(multiplexer_129_out[5]), .in1(multiplexer_129_out[6]), .out(multiplexer_161_out[5]),
    .sel(PLA_1_out[5]));
  Multiplexer multiplexer_167 (
    .in0(multiplexer_129_out[6]), .in1(multiplexer_129_out[7]), .out(multiplexer_161_out[6]),
    .sel(PLA_1_out[5]));
  Multiplexer multiplexer_168 (
    .in0(multiplexer_129_out[7]), .in1(multiplexer_129_out[8]), .out(multiplexer_161_out[7]),
    .sel(PLA_1_out[5]));
  Multiplexer multiplexer_169 (
    .in0(multiplexer_129_out[8]), .in1(multiplexer_129_out[9]), .out(multiplexer_161_out[8]),
    .sel(PLA_1_out[5]));
  Multiplexer multiplexer_170 (
    .in0(multiplexer_129_out[9]), .in1(multiplexer_129_out[10]), .out(multiplexer_161_out[9]),
    .sel(PLA_1_out[5]));
  Multiplexer multiplexer_171 (
    .in0(multiplexer_129_out[10]), .in1(multiplexer_129_out[11]), .out(multiplexer_161_out[10]),
    .sel(PLA_1_out[5]));
  Multiplexer multiplexer_172 (
    .in0(multiplexer_129_out[11]), .in1(multiplexer_129_out[12]), .out(multiplexer_161_out[11]),
    .sel(PLA_1_out[5]));
  Multiplexer multiplexer_173 (
    .in0(multiplexer_129_out[12]), .in1(multiplexer_129_out[13]), .out(multiplexer_161_out[12]),
    .sel(PLA_1_out[5]));
  Multiplexer multiplexer_174 (
    .in0(multiplexer_129_out[13]), .in1(multiplexer_129_out[14]), .out(multiplexer_161_out[13]),
    .sel(PLA_1_out[5]));
  Multiplexer multiplexer_175 (
    .in0(multiplexer_129_out[14]), .in1(multiplexer_129_out[15]), .out(multiplexer_161_out[14]),
    .sel(PLA_1_out[5]));
  Multiplexer multiplexer_176 (
    .in0(multiplexer_129_out[15]), .in1(1'b0), .out(multiplexer_161_out[15]), .sel(PLA_1_out[5]));
  and and_12 (and_12_out, multiplexer_145_out[0], PLA_1_out[13]);
  Multiplexer multiplexer_177 (
    .in0(multiplexer_145_out[0]), .in1(multiplexer_145_out[1]), .out(multiplexer_177_out[0]),
    .sel(PLA_1_out[13]));
  Multiplexer multiplexer_178 (
    .in0(multiplexer_145_out[1]), .in1(multiplexer_145_out[2]), .out(multiplexer_177_out[1]),
    .sel(PLA_1_out[13]));
  Multiplexer multiplexer_179 (
    .in0(multiplexer_145_out[2]), .in1(multiplexer_145_out[3]), .out(multiplexer_177_out[2]),
    .sel(PLA_1_out[13]));
  Multiplexer multiplexer_180 (
    .in0(multiplexer_145_out[3]), .in1(multiplexer_145_out[4]), .out(multiplexer_177_out[3]),
    .sel(PLA_1_out[13]));
  Multiplexer multiplexer_181 (
    .in0(multiplexer_145_out[4]), .in1(multiplexer_145_out[5]), .out(multiplexer_177_out[4]),
    .sel(PLA_1_out[13]));
  Multiplexer multiplexer_182 (
    .in0(multiplexer_145_out[5]), .in1(multiplexer_145_out[6]), .out(multiplexer_177_out[5]),
    .sel(PLA_1_out[13]));
  Multiplexer multiplexer_183 (
    .in0(multiplexer_145_out[6]), .in1(multiplexer_145_out[7]), .out(multiplexer_177_out[6]),
    .sel(PLA_1_out[13]));
  Multiplexer multiplexer_184 (
    .in0(multiplexer_145_out[7]), .in1(multiplexer_145_out[8]), .out(multiplexer_177_out[7]),
    .sel(PLA_1_out[13]));
  Multiplexer multiplexer_185 (
    .in0(multiplexer_145_out[8]), .in1(multiplexer_145_out[9]), .out(multiplexer_177_out[8]),
    .sel(PLA_1_out[13]));
  Multiplexer multiplexer_186 (
    .in0(multiplexer_145_out[9]), .in1(multiplexer_145_out[10]), .out(multiplexer_177_out[9]),
    .sel(PLA_1_out[13]));
  Multiplexer multiplexer_187 (
    .in0(multiplexer_145_out[10]), .in1(multiplexer_145_out[11]), .out(multiplexer_177_out[10]),
    .sel(PLA_1_out[13]));
  Multiplexer multiplexer_188 (
    .in0(multiplexer_145_out[11]), .in1(multiplexer_145_out[12]), .out(multiplexer_177_out[11]),
    .sel(PLA_1_out[13]));
  Multiplexer multiplexer_189 (
    .in0(multiplexer_145_out[12]), .in1(multiplexer_145_out[13]), .out(multiplexer_177_out[12]),
    .sel(PLA_1_out[13]));
  Multiplexer multiplexer_190 (
    .in0(multiplexer_145_out[13]), .in1(multiplexer_145_out[14]), .out(multiplexer_177_out[13]),
    .sel(PLA_1_out[13]));
  Multiplexer multiplexer_191 (
    .in0(multiplexer_145_out[14]), .in1(multiplexer_145_out[15]), .out(multiplexer_177_out[14]),
    .sel(PLA_1_out[13]));
  Multiplexer multiplexer_192 (
    .in0(multiplexer_145_out[15]), .in1(1'b0), .out(multiplexer_177_out[15]), .sel(PLA_1_out[13]));
  and and_13 (and_13_out, multiplexer_161_out[0], PLA_1_out[6]);
  and and_14 (and_14_out, multiplexer_177_out[0], PLA_1_out[14]);
  Multiplexer multiplexer_193 (
    .in0(multiplexer_161_out[0]), .in1(multiplexer_161_out[1]), .out(multiplexer_193_out[0]),
    .sel(PLA_1_out[6]));
  Multiplexer multiplexer_194 (
    .in0(multiplexer_161_out[1]), .in1(multiplexer_161_out[2]), .out(multiplexer_193_out[1]),
    .sel(PLA_1_out[6]));
  Multiplexer multiplexer_195 (
    .in0(multiplexer_161_out[2]), .in1(multiplexer_161_out[3]), .out(multiplexer_193_out[2]),
    .sel(PLA_1_out[6]));
  Multiplexer multiplexer_196 (
    .in0(multiplexer_161_out[3]), .in1(multiplexer_161_out[4]), .out(multiplexer_193_out[3]),
    .sel(PLA_1_out[6]));
  Multiplexer multiplexer_197 (
    .in0(multiplexer_161_out[4]), .in1(multiplexer_161_out[5]), .out(multiplexer_193_out[4]),
    .sel(PLA_1_out[6]));
  Multiplexer multiplexer_198 (
    .in0(multiplexer_161_out[5]), .in1(multiplexer_161_out[6]), .out(multiplexer_193_out[5]),
    .sel(PLA_1_out[6]));
  Multiplexer multiplexer_199 (
    .in0(multiplexer_161_out[6]), .in1(multiplexer_161_out[7]), .out(multiplexer_193_out[6]),
    .sel(PLA_1_out[6]));
  Multiplexer multiplexer_200 (
    .in0(multiplexer_161_out[7]), .in1(multiplexer_161_out[8]), .out(multiplexer_193_out[7]),
    .sel(PLA_1_out[6]));
  Multiplexer multiplexer_201 (
    .in0(multiplexer_161_out[8]), .in1(multiplexer_161_out[9]), .out(multiplexer_193_out[8]),
    .sel(PLA_1_out[6]));
  Multiplexer multiplexer_202 (
    .in0(multiplexer_161_out[9]), .in1(multiplexer_161_out[10]), .out(multiplexer_193_out[9]),
    .sel(PLA_1_out[6]));
  Multiplexer multiplexer_203 (
    .in0(multiplexer_161_out[10]), .in1(multiplexer_161_out[11]), .out(multiplexer_193_out[10]),
    .sel(PLA_1_out[6]));
  Multiplexer multiplexer_204 (
    .in0(multiplexer_161_out[11]), .in1(multiplexer_161_out[12]), .out(multiplexer_193_out[11]),
    .sel(PLA_1_out[6]));
  Multiplexer multiplexer_205 (
    .in0(multiplexer_161_out[12]), .in1(multiplexer_161_out[13]), .out(multiplexer_193_out[12]),
    .sel(PLA_1_out[6]));
  Multiplexer multiplexer_206 (
    .in0(multiplexer_161_out[13]), .in1(multiplexer_161_out[14]), .out(multiplexer_193_out[13]),
    .sel(PLA_1_out[6]));
  Multiplexer multiplexer_207 (
    .in0(multiplexer_161_out[14]), .in1(multiplexer_161_out[15]), .out(multiplexer_193_out[14]),
    .sel(PLA_1_out[6]));
  Multiplexer multiplexer_208 (
    .in0(multiplexer_161_out[15]), .in1(1'b0), .out(multiplexer_193_out[15]), .sel(PLA_1_out[6]));
  Multiplexer multiplexer_209 (
    .in0(multiplexer_177_out[0]), .in1(multiplexer_177_out[1]), .out(Output_bus_1[0]), .sel(PLA_1_out[14]));
  Multiplexer multiplexer_210 (
    .in0(multiplexer_177_out[1]), .in1(multiplexer_177_out[2]), .out(Output_bus_1[1]), .sel(PLA_1_out[14]));
  Multiplexer multiplexer_211 (
    .in0(multiplexer_177_out[2]), .in1(multiplexer_177_out[3]), .out(Output_bus_1[2]), .sel(PLA_1_out[14]));
  Multiplexer multiplexer_212 (
    .in0(multiplexer_177_out[3]), .in1(multiplexer_177_out[4]), .out(Output_bus_1[3]), .sel(PLA_1_out[14]));
  Multiplexer multiplexer_213 (
    .in0(multiplexer_177_out[4]), .in1(multiplexer_177_out[5]), .out(Output_bus_1[4]), .sel(PLA_1_out[14]));
  Multiplexer multiplexer_214 (
    .in0(multiplexer_177_out[5]), .in1(multiplexer_177_out[6]), .out(Output_bus_1[5]), .sel(PLA_1_out[14]));
  Multiplexer multiplexer_215 (
    .in0(multiplexer_177_out[6]), .in1(multiplexer_177_out[7]), .out(Output_bus_1[6]), .sel(PLA_1_out[14]));
  Multiplexer multiplexer_216 (
    .in0(multiplexer_177_out[7]), .in1(multiplexer_177_out[8]), .out(Output_bus_1[7]), .sel(PLA_1_out[14]));
  Multiplexer multiplexer_217 (
    .in0(multiplexer_177_out[8]), .in1(multiplexer_177_out[9]), .out(Output_bus_1[8]), .sel(PLA_1_out[14]));
  Multiplexer multiplexer_218 (
    .in0(multiplexer_177_out[9]), .in1(multiplexer_177_out[10]), .out(Output_bus_1[9]), .sel(PLA_1_out[14]));
  Multiplexer multiplexer_219 (
    .in0(multiplexer_177_out[10]), .in1(multiplexer_177_out[11]), .out(Output_bus_1[10]), .sel(PLA_1_out[14]));
  Multiplexer multiplexer_220 (
    .in0(multiplexer_177_out[11]), .in1(multiplexer_177_out[12]), .out(Output_bus_1[11]), .sel(PLA_1_out[14]));
  Multiplexer multiplexer_221 (
    .in0(multiplexer_177_out[12]), .in1(multiplexer_177_out[13]), .out(Output_bus_1[12]), .sel(PLA_1_out[14]));
  Multiplexer multiplexer_222 (
    .in0(multiplexer_177_out[13]), .in1(multiplexer_177_out[14]), .out(Output_bus_1[13]), .sel(PLA_1_out[14]));
  Multiplexer multiplexer_223 (
    .in0(multiplexer_177_out[14]), .in1(multiplexer_177_out[15]), .out(Output_bus_1[14]), .sel(PLA_1_out[14]));
  Multiplexer multiplexer_224 (.in0(multiplexer_177_out[15]), .in1(1'b0), .out(Output_bus_1[15]), .sel(PLA_1_out[14]));
  or or_1 (or_1_out, and_4_out, and_6_out, and_8_out, and_2_out, and_12_out, and_14_out, and_10_out);
  and and_15 (and_15_out, multiplexer_193_out[0], PLA_1_out[7]);
  Multiplexer multiplexer_225 (
    .in0(multiplexer_193_out[0]), .in1(multiplexer_193_out[1]), .out(multiplexer_225_out[0]),
    .sel(PLA_1_out[7]));
  Multiplexer multiplexer_226 (
    .in0(multiplexer_193_out[1]), .in1(multiplexer_193_out[2]), .out(multiplexer_225_out[1]),
    .sel(PLA_1_out[7]));
  Multiplexer multiplexer_227 (
    .in0(multiplexer_193_out[2]), .in1(multiplexer_193_out[3]), .out(multiplexer_225_out[2]),
    .sel(PLA_1_out[7]));
  Multiplexer multiplexer_228 (
    .in0(multiplexer_193_out[3]), .in1(multiplexer_193_out[4]), .out(multiplexer_225_out[3]),
    .sel(PLA_1_out[7]));
  Multiplexer multiplexer_229 (
    .in0(multiplexer_193_out[4]), .in1(multiplexer_193_out[5]), .out(multiplexer_225_out[4]),
    .sel(PLA_1_out[7]));
  Multiplexer multiplexer_230 (
    .in0(multiplexer_193_out[5]), .in1(multiplexer_193_out[6]), .out(multiplexer_225_out[5]),
    .sel(PLA_1_out[7]));
  Multiplexer multiplexer_231 (
    .in0(multiplexer_193_out[6]), .in1(multiplexer_193_out[7]), .out(multiplexer_225_out[6]),
    .sel(PLA_1_out[7]));
  Multiplexer multiplexer_232 (
    .in0(multiplexer_193_out[7]), .in1(multiplexer_193_out[8]), .out(multiplexer_225_out[7]),
    .sel(PLA_1_out[7]));
  Multiplexer multiplexer_233 (
    .in0(multiplexer_193_out[8]), .in1(multiplexer_193_out[9]), .out(multiplexer_225_out[8]),
    .sel(PLA_1_out[7]));
  Multiplexer multiplexer_234 (
    .in0(multiplexer_193_out[9]), .in1(multiplexer_193_out[10]), .out(multiplexer_225_out[9]),
    .sel(PLA_1_out[7]));
  Multiplexer multiplexer_235 (
    .in0(multiplexer_193_out[10]), .in1(multiplexer_193_out[11]), .out(multiplexer_225_out[10]),
    .sel(PLA_1_out[7]));
  Multiplexer multiplexer_236 (
    .in0(multiplexer_193_out[11]), .in1(multiplexer_193_out[12]), .out(multiplexer_225_out[11]),
    .sel(PLA_1_out[7]));
  Multiplexer multiplexer_237 (
    .in0(multiplexer_193_out[12]), .in1(multiplexer_193_out[13]), .out(multiplexer_225_out[12]),
    .sel(PLA_1_out[7]));
  Multiplexer multiplexer_238 (
    .in0(multiplexer_193_out[13]), .in1(multiplexer_193_out[14]), .out(multiplexer_225_out[13]),
    .sel(PLA_1_out[7]));
  Multiplexer multiplexer_239 (
    .in0(multiplexer_193_out[14]), .in1(multiplexer_193_out[15]), .out(multiplexer_225_out[14]),
    .sel(PLA_1_out[7]));
  Multiplexer multiplexer_240 (
    .in0(multiplexer_193_out[15]), .in1(1'b0), .out(multiplexer_225_out[15]), .sel(PLA_1_out[7]));
  or or_2 (or_2_out, and_1_out, and_3_out, and_5_out, and_7_out, and_11_out, and_13_out, and_15_out, and_9_out);
  or or_3 (carry_out, or_2_out, or_1_out);
endmodule

module Instruction_Control (
  input  [15:0] mem_data_in,
  input  [15:0] mem_addr_in,
  input  CLK,
  input  [15:0] pc_data_in,
  input  pc_write_enable,
  input  carry_flag,
  input  zero_flag,
  input  sign_flag,
  input  RESET,
  output [15:0] mem_data_out,
  output [15:0] operand,
  output [15:0] pc_data_out,
  output [18:0] CPU_Control_BUS
);

  wire and_1_out, and_2_out, and_3_out, comparator_1_eq, comparator_1_gt, comparator_2_eq, comparator_3_eq,
       not_1_out, not_2_out, or_1_out, or_3_out;
  wire [7:0] IDSC_q, ITSD_out, subtractor_1_out, TSR_q;
  wire [15:0] adder_1_out, adder_2_out, bit_extender_1_out, IMBD_out, Instruction_Register_p4,
       Instruction_Register_p5, MOR_q, multiplexer_1_out;
  wire [16:16] or_2_out;
  wire [23:0] Microcode_ROM_data, multiplexer_3_out;

  and and_1 (and_1_out, CLK, not_1_out);
  Counter #(.max('hffff), .width(16)) PC (
    .clr(RESET), .clk(and_1_out), .D(pc_data_in), .Q(pc_data_out));  // open: load, up, count, carry
  not not_1 (not_1_out, or_2_out[16]);
  LedBar #(.matrixcols(16)) LedBar_4 (
    .led0(pc_data_out[15]), .led1(pc_data_out[14]), .led2(pc_data_out[13]), .led3(pc_data_out[12]),
    .led4(pc_data_out[11]), .led5(pc_data_out[10]), .led6(pc_data_out[9]), .led7(pc_data_out[8]),
    .led8(pc_data_out[7]), .led9(pc_data_out[6]), .led10(pc_data_out[5]), .led11(pc_data_out[4]),
    .led12(pc_data_out[3]), .led13(pc_data_out[2]), .led14(pc_data_out[1]), .led15(pc_data_out[0]));
  Adder #(.width(16)) adder_1 (
    .a(mem_addr_in), .b(Instruction_Register_p4), .out(adder_1_out), .cin(1'b0));  // open: cout
  Multiplexer #(.select(2), .width(16)) multiplexer_1 (
    .in0(pc_data_out), .in1(adder_1_out), .in2(Instruction_Register_p4), .out(multiplexer_1_out),
    .sel(CPU_Control_BUS[1:0]));  // open: in3
  RAM #(.addrWidth(16), .dataWidth(16), .enables("line")) RAM_1 (
    .addr(multiplexer_1_out), .we(multiplexer_3_out[0]), .clk(CLK), .din(mem_data_in), .dout(mem_data_out));
  or or_1 (or_1_out, RESET, and_2_out);
  Counter IDSC (.clr(or_1_out), .clk(CLK), .Q(IDSC_q));  // open: load, up, count, D, carry
  // Shift_Register #(.length(2), .width(16)) Instruction_Register: pin names not known; wires that end beside it: RESET, and_1_out, mem_data_out, Instruction_Register_p4, Instruction_Register_p5
  and and_2 (and_2_out, or_3_out, comparator_3_eq);
  PLA #(.in_width(16), .out_width(8)) ITSD (.in(Instruction_Register_p4), .out(ITSD_out));
  Comparator #(.mode("unsigned")) comparator_1 (
    .a(IDSC_q), .b(8'h2), .gt(comparator_1_gt), .eq(comparator_1_eq));  // open: lt
  or or_2 (or_2_out[16], comparator_1_gt, comparator_1_eq);
  Comparator #(.mode("unsigned")) comparator_2 (.a(8'h1), .b(IDSC_q), .eq(comparator_2_eq));  // open: gt, lt
  or or_3 (or_3_out, IDSC_q[0], IDSC_q[1], IDSC_q[2], IDSC_q[3], IDSC_q[4], IDSC_q[5], IDSC_q[6], IDSC_q[7]);
  Subtractor subtractor_1 (.a(IDSC_q), .b(8'h1), .out(subtractor_1_out));  // open: bin, bout
  Multiplexer #(.width(16)) multiplexer_2 (
    .in0(Instruction_Register_p5), .in1(MOR_q), .out(operand), .sel(multiplexer_3_out[20]));
  PLA #(.in_width(20), .out_width(16)) IMBD (
    .in({carry_flag, zero_flag, sign_flag, or_2_out[16], Instruction_Register_p4}), .out(IMBD_out));
  Register TSR (.D(ITSD_out), .en(comparator_2_eq), .clk(CLK), .Q(TSR_q), .clr(RESET));
  Comparator #(.mode("unsigned")) comparator_3 (.a(TSR_q), .b(IDSC_q), .eq(comparator_3_eq));  // open: gt, lt
  Adder #(.width(16)) adder_2 (.a(IMBD_out), .b(bit_extender_1_out), .out(adder_2_out));  // open: cin, cout
  assign bit_extender_1_out = {{8{1'b0}}, subtractor_1_out};  // Bit_Extender bit_extender_1
  ROM #(.addrWidth(16), .dataWidth(24)) Microcode_ROM (.addr(adder_2_out), .data(Microcode_ROM_data));
  Multiplexer #(.width(24)) multiplexer_3 (
    .in0(24'h78), .in1(Microcode_ROM_data),
    .out({multiplexer_3_out[23:20], CPU_Control_BUS, multiplexer_3_out[0]}), .sel(and_3_out));
  and and_3 (and_3_out, or_2_out[16], not_2_out);
  not not_2 (not_2_out, multiplexer_3_out[21]);
  Register #(.width(16)) MOR (
    .D({CPU_Control_BUS[14:0], multiplexer_3_out[0]}), .en(multiplexer_3_out[21]), .clk(CLK), .Q(MOR_q),
    .clr(RESET));
endmodule

module registers (
  input  [15:0] reg_data_in,
  input  CLK,
  input  RESET,
  input  [15:0] write_reg_select,
  input  carry_flag,
  input  zero_flag,
  input  sign_flag,
  input  flag_write_sw,
  output [15:0] memval_out,
  output [15:0] memaddr_out,
  output [15:0] a_out,
  output [15:0] b_out,
  output [15:0] c_out,
  output [15:0] d_out,
  output [15:0] e_out,
  output [15:0] bp_out,
  output [15:0] sp_out,
  output [15:0] output_out,
  output [15:0] flag_output
);

  wire or_1_out;
  wire [15:0] multiplexer_1_out;

  Register #(.width(16)) MEMVAL (.D(reg_data_in), .en(write_reg_select[10]), .clk(CLK), .Q(memval_out), .clr(RESET));
  Register #(.width(16)) MEMADDR (.D(reg_data_in), .en(write_reg_select[9]), .clk(CLK), .Q(memaddr_out), .clr(RESET));
  Register #(.width(16)) A (.D(reg_data_in), .en(write_reg_select[0]), .clk(CLK), .Q(a_out), .clr(RESET));
  Register #(.width(16)) B (.D(reg_data_in), .en(write_reg_select[1]), .clk(CLK), .Q(b_out), .clr(RESET));
  Register #(.width(16)) C (.D(reg_data_in), .en(write_reg_select[2]), .clk(CLK), .Q(c_out), .clr(RESET));
  Register #(.width(16)) D (.D(reg_data_in), .en(write_reg_select[3]), .clk(CLK), .Q(d_out), .clr(RESET));
  Register #(.width(16)) E (.D(reg_data_in), .en(write_reg_select[4]), .clk(CLK), .Q(e_out), .clr(RESET));
  Register #(.width(16)) BP (.D(reg_data_in), .en(write_reg_select[5]), .clk(CLK), .Q(bp_out), .clr(RESET));
  Register #(.width(16)) SP (.D(reg_data_in), .en(write_reg_select[6]), .clk(CLK), .Q(sp_out), .clr(RESET));
  Register #(.width(16)) Output_port (
    .D(reg_data_in), .en(write_reg_select[8]), .clk(CLK), .Q(output_out), .clr(RESET));
  Multiplexer #(.width(16)) multiplexer_1 (
    .in0(reg_data_in), .in1({flag_output[15:3], sign_flag, zero_flag, carry_flag}), .out(multiplexer_1_out),
    .sel(flag_write_sw));
  or or_1 (or_1_out, write_reg_select[11], flag_write_sw);
  Register #(.width(16)) FLAGS (.D(multiplexer_1_out), .en(or_1_out), .clk(CLK), .Q(flag_output), .clr(RESET));
endmodule

module ALU (
  input  [15:0] in1_data_in,
  input  [15:0] in2_data_in,
  input  [2:0] ALU_function_select,
  output [15:0] ALU_Out,
  output sign_flag,
  output zero_flag,
  output carry_flag
);

  wire adder_1_cout, not_2_out, not_3_out, not_4_out, not_5_out, not_6_out, not_7_out, not_8_out, not_9_out,
       not_10_out, not_11_out, not_12_out, not_13_out, not_14_out, not_15_out, not_16_out, not_17_out,
       right_shifter_1_carry_out;
  wire [15:0] adder_1_out, and_1_out, demultiplexer_1_out0, demultiplexer_1_out1, demultiplexer_1_out2,
       demultiplexer_1_out3, demultiplexer_1_out4, demultiplexer_1_out5, demultiplexer_1_out6,
       demultiplexer_1_out7, demultiplexer_2_out0, demultiplexer_2_out1, demultiplexer_2_out2,
       demultiplexer_2_out3, demultiplexer_2_out4, demultiplexer_2_out6, demultiplexer_2_out7,
       multiplier_1_cout, multiplier_1_out, not_1_out, or_1_out, right_shifter_1_output_bus_1,
       subtractor_1_out, xor_1_out;

  Demultiplexer #(.select(3), .width(16)) demultiplexer_1 (
    .out0(demultiplexer_1_out0), .out1(demultiplexer_1_out1), .out2(demultiplexer_1_out2),
    .out3(demultiplexer_1_out3), .out4(demultiplexer_1_out4), .out5(demultiplexer_1_out5),
    .out6(demultiplexer_1_out6), .out7(demultiplexer_1_out7), .in(in1_data_in), .sel(ALU_function_select));
  Demultiplexer #(.select(3), .width(16)) demultiplexer_2 (
    .out0(demultiplexer_2_out0), .out1(demultiplexer_2_out1), .out2(demultiplexer_2_out2),
    .out3(demultiplexer_2_out3), .out4(demultiplexer_2_out4), .out6(demultiplexer_2_out6),
    .out7(demultiplexer_2_out7), .in(in2_data_in), .sel(ALU_function_select));  // open: out5
  Adder #(.width(16)) adder_1 (
    .a(demultiplexer_1_out0), .b(demultiplexer_2_out0), .out(adder_1_out), .cin(1'b0), .cout(adder_1_cout));
  Subtractor #(.width(16)) subtractor_1 (
    .a(demultiplexer_1_out1), .b(demultiplexer_2_out1), .out(subtractor_1_out), .bin(1'b0), .bout(sign_flag));
  Multiplier #(.width(16)) multiplier_1 (
    .a(demultiplexer_1_out2), .b(demultiplexer_2_out2), .out(multiplier_1_out), .cin({16{1'b0}}),
    .cout(multiplier_1_cout));
  assign and_1_out = demultiplexer_1_out3 & demultiplexer_2_out3;  // AND_Gate and_1, 16 bits wide
  assign or_1_out = demultiplexer_1_out4 | demultiplexer_2_out4;  // OR_Gate or_1, 16 bits wide
  assign not_1_out = ~demultiplexer_1_out5;  // NOT_Gate not_1, 16 bits wide
  assign xor_1_out = demultiplexer_1_out6 ^ demultiplexer_2_out6;  // XOR_Gate xor_1, 16 bits wide
  right_shifter right_shifter_1 (
    .Input_bus_1(demultiplexer_2_out7), .Input_bus_2(demultiplexer_1_out7),
    .carry_out(right_shifter_1_carry_out), .Output_bus_1(right_shifter_1_output_bus_1));
  Multiplexer #(.select(3), .width(16)) multiplexer_1 (
    .in0(adder_1_out), .in1(subtractor_1_out), .in2(multiplier_1_out), .in3(and_1_out), .in4(or_1_out),
    .in5(not_1_out), .in6(xor_1_out), .in7(right_shifter_1_output_bus_1), .out(ALU_Out),
    .sel(ALU_function_select));
  or or_2 (carry_flag, adder_1_cout, multiplier_1_cout[7], multiplier_1_cout[0], multiplier_1_cout[1], multiplier_1_cout[2], multiplier_1_cout[3], multiplier_1_cout[4], multiplier_1_cout[5], multiplier_1_cout[6], multiplier_1_cout[8], multiplier_1_cout[9], multiplier_1_cout[10], multiplier_1_cout[11], multiplier_1_cout[12], multiplier_1_cout[13], multiplier_1_cout[14], multiplier_1_cout[15], right_shifter_1_carry_out);
  not not_2 (not_2_out, ALU_Out[0]);
  not not_3 (not_3_out, ALU_Out[1]);
  not not_4 (not_4_out, ALU_Out[2]);
  not not_5 (not_5_out, ALU_Out[3]);
  not not_6 (not_6_out, ALU_Out[4]);
  not not_7 (not_7_out, ALU_Out[5]);
  not not_8 (not_8_out, ALU_Out[6]);
  not not_9 (not_9_out, ALU_Out[7]);
  not not_10 (not_10_out, ALU_Out[8]);
  not not_11 (not_11_out, ALU_Out[9]);
  not not_12 (not_12_out, ALU_Out[10]);
  not not_13 (not_13_out, ALU_Out[11]);
  not not_14 (not_14_out, ALU_Out[12]);
  not not_15 (not_15_out, ALU_Out[13]);
  not not_16 (not_16_out, ALU_Out[14]);
  not not_17 (not_17_out, ALU_Out[15]);
  and and_2 (zero_flag, not_9_out, not_2_out, not_3_out, not_4_out, not_5_out, not_6_out, not_7_out, not_8_out, not_10_out, not_11_out, not_12_out, not_13_out, not_14_out, not_15_out, not_16_out, not_17_out);
endmodule
